# Fritzing sketch MyStandingDesk (saved by Fritzing 0.9.2b)
breadboards: 1

parts:
  부품1 = Arduino Uno (Rev3)
  부품2 = Bluetooth HC-06
  KY-1 = Keyes Relay [package=THT]
  KY-2 = Keyes Relay [package=THT]
  부품3 = HC-SR 04

nets:
  N1: 부품1.D8, KY-1.signal
  N2: 부품1.D9_PWM, KY-2.signal
  N3: 부품1.D10_PWM/SS, 부품3.Trig
  N4: 부품1.D11_PWM/MOSI, 부품3.Echo
  N5: 부품1.D0/RX, 부품2.TXD
  N6: 부품1.D1/TX, 부품2.RXD
  VCC: 부품1.5V, 부품2.VCC, KY-1.power, KY-2.power, 부품3.VCC
  GND: 부품1.GND, 부품2.GND, KY-1.ground, KY-2.ground, 부품3.GND
  N7: KY-1.NO, KY-2.NO

notes:
  [Standing Desk Control]
  GND
  [Standing Desk Control]
  Up button signal
  [Standing Desk Control]
  Down button signal

custom parts:
  Keyes Relay: The Keyes 5V relay module is suitable for SCM development, home appliance control. It uses a 5V~12V TIL control signal which can control DC / AC signal.
